// Logisim project volcano_monitor.circ as structural Verilog: 1 circuit, main circuit main
module main (
  input  [7:0] VIB,
  input  [7:0] TMP,
  input  [7:0] GAS,
  input  [7:0] ACT,
  output OUT_WATCH,
  output OUT_DANGER,
  output OUT_EMERG,
  output [3:0] OUT_DCNT,
  output [3:0] OUT_ABN
);

  wire and_1_out, and_2_out, and_3_out, and_4_out, and_5_out, CLK, comparator_1_lt, comparator_2_lt,
       comparator_3_lt, comparator_4_lt, comparator_5_lt, comparator_6_lt, comparator_7_lt, comparator_8_lt,
       comparator_9_lt, DACT, DGAS, DTMP, DVIB, not_1_out, not_2_out, not_12_out, not_13_out, not_14_out,
       not_15_out, not_16_out, not_17_out, not_18_out, not_19_out, or_1_out, or_2_out, or_3_out, or_4_out,
       WACT, WEND, WGAS, WTMP, WVIB;
  wire [3:0] adder_1_out, adder_2_out, bit_extender_1_out, bit_extender_2_out, bit_extender_3_out,
       bit_extender_4_out, WINC;
  wire [3:1] undriven, undriven_2;

  Clock SAMPLE_CLOCK (.out(CLK));
  or or_1 (or_1_out, WVIB, WTMP);
  or or_2 (or_2_out, WGAS, WACT);
  or or_3 (or_3_out, DVIB, DTMP);
  or or_4 (or_4_out, DGAS, DACT);
  not not_1 (not_1_out, OUT_WATCH);
  LED SYS_NORMAL (.in(not_1_out));
  LED SYS_DANGER (.in(OUT_DANGER));
  and and_1 (and_1_out, OUT_WATCH, not_2_out);
  not not_2 (not_2_out, OUT_DANGER);
  assign bit_extender_1_out = {{3{1'b0}}, DVIB};  // Bit_Extender bit_extender_1
  assign bit_extender_2_out = {{3{1'b0}}, DTMP};  // Bit_Extender bit_extender_2
  assign bit_extender_3_out = {{3{1'b0}}, DGAS};  // Bit_Extender bit_extender_3
  assign bit_extender_4_out = {{3{1'b0}}, DACT};  // Bit_Extender bit_extender_4
  Comparator #(.width(4), .mode("unsigned")) comparator_1 (
    .a(OUT_DCNT), .b(4'b0010), .lt(comparator_1_lt));  // open: gt, eq
  LED ALARM_LED (.in(OUT_EMERG));
  // Buzzer SIREN: pin names not known; wires that end beside it: OUT_EMERG, 1'b0, 1'b0
  Hex_Digit_Display HEX_WINDOW (.value(WINC));  // open: dp
  Hex_Digit_Display HEX_ABNORMAL (.value(OUT_ABN));  // open: dp
  LED SYS_WATCH (.in(and_1_out));
  Adder #(.width(4)) adder_1 (.a(bit_extender_1_out), .b(bit_extender_2_out), .out(adder_1_out));  // open: cin, cout
  Adder #(.width(4)) adder_2 (.a(bit_extender_3_out), .b(bit_extender_4_out), .out(adder_2_out));  // open: cin, cout
  not not_3 (OUT_EMERG, comparator_1_lt);
  Counter #(.width(4), .max('h8)) CNT_WINDOW (
    .load(1'b0), .D({undriven, 1'b0}), .count(1'b1), .Q(WINC), .carry(WEND), .up(1'b0), .clk(CLK), .clr(1'b0));
  or or_5 (OUT_WATCH, or_1_out, or_2_out);
  or or_6 (OUT_DANGER, or_3_out, or_4_out);
  Adder #(.width(4)) adder_3 (.a(adder_1_out), .b(adder_2_out), .out(OUT_DCNT), .cin(1'b0));  // open: cout
  Counter #(.width(4), .max('hf)) CNT_ABNORMAL (
    .load(1'b0), .D({undriven_2, 1'b0}), .count(OUT_WATCH), .Q(OUT_ABN), .up(1'b0), .clk(CLK), .clr(WEND));  // open: carry
  Comparator #(.mode("unsigned")) comparator_2 (.a(VIB), .b(8'h28), .lt(comparator_2_lt));  // open: gt, eq
  Comparator #(.mode("unsigned")) comparator_3 (.a(VIB), .b(8'h46), .lt(comparator_3_lt));  // open: gt, eq
  Comparator #(.mode("unsigned")) comparator_4 (.a(TMP), .b(8'h3c), .lt(comparator_4_lt));  // open: gt, eq
  Comparator #(.mode("unsigned")) comparator_5 (.a(TMP), .b(8'h55), .lt(comparator_5_lt));  // open: gt, eq
  Comparator #(.mode("unsigned")) comparator_6 (.a(GAS), .b(8'h64), .lt(comparator_6_lt));  // open: gt, eq
  Comparator #(.mode("unsigned")) comparator_7 (.a(GAS), .b(8'hb4), .lt(comparator_7_lt));  // open: gt, eq
  Comparator #(.mode("unsigned")) comparator_8 (.a(ACT), .b(8'h32), .lt(comparator_8_lt));  // open: gt, eq
  Comparator #(.mode("unsigned")) comparator_9 (.a(ACT), .b(8'h50), .lt(comparator_9_lt));  // open: gt, eq
  not not_4 (WVIB, comparator_2_lt);
  not not_5 (DVIB, comparator_3_lt);
  not not_6 (WTMP, comparator_4_lt);
  not not_7 (DTMP, comparator_5_lt);
  not not_8 (WGAS, comparator_6_lt);
  not not_9 (DGAS, comparator_7_lt);
  not not_10 (WACT, comparator_8_lt);
  not not_11 (DACT, comparator_9_lt);
  Hex_Digit_Display HEX_DANGER_COUNT (.value(OUT_DCNT));  // open: dp
  not not_12 (not_12_out, WVIB);
  LED LEDN_VIB (.in(not_12_out));
  not not_13 (not_13_out, DVIB);
  LED LEDD_VIB (.in(DVIB));
  not not_14 (not_14_out, WTMP);
  LED LEDN_TMP (.in(not_14_out));
  not not_15 (not_15_out, DTMP);
  LED LEDD_TMP (.in(DTMP));
  not not_16 (not_16_out, WGAS);
  LED LEDN_GAS (.in(not_16_out));
  not not_17 (not_17_out, DGAS);
  LED LEDD_GAS (.in(DGAS));
  not not_18 (not_18_out, WACT);
  LED LEDN_ACT (.in(not_18_out));
  not not_19 (not_19_out, DACT);
  LED LEDD_ACT (.in(DACT));
  and and_2 (and_2_out, WVIB, not_13_out);
  LED LEDW_VIB (.in(and_2_out));
  and and_3 (and_3_out, WTMP, not_15_out);
  LED LEDW_TMP (.in(and_3_out));
  and and_4 (and_4_out, WGAS, not_17_out);
  LED LEDW_GAS (.in(and_4_out));
  and and_5 (and_5_out, WACT, not_19_out);
  LED LEDW_ACT (.in(and_5_out));
  // Pins of 1 and 4 bits meet at {undriven, 1'b0}
  // Pins of 1 and 4 bits meet at {undriven_2, 1'b0}

  // Other names for the same wires on the sheet: ABN[3:0] = OUT_ABN; DANY = OUT_DANGER; DCNT[3:0] = OUT_DCNT;
  //   EMERG = OUT_EMERG; SACT[7:0] = ACT; SGAS[7:0] = GAS; STMP[7:0] = TMP; SVIB[7:0] = VIB; WANY = OUT_WATCH
endmodule
